// Logisim project Binary_to_BCD_Converter_Logisim_Evolution (3).circ as structural Verilog: 1 circuit, main circuit main
// 4-bit Binary to BCD Converter
module main (
  input  A__8,
  input  B__4,
  input  C__2,
  input  D__1,
  output Tens_T,
  output Units_U3__0,
  output Units_U2,
  output Units_U1,
  output Units_U0
);

  wire not_1_out, or_1_out, or_2_out, xor_1_p1;

  or or_1 (or_1_out, B__4, C__2);
  // AND_Gate and_1 has open pins: out=Tens_T
  not not_1 (not_1_out, xor_1_p1);
  // OR_Gate or_2 has open pins: out=or_2_out
  // XOR_Gate xor_1: pin names not known; wires that end beside it: xor_1_p1, C__2, Units_U1
  and and_2 (Units_U2, or_2_out, B__4);

  assign Units_U0 = D__1;
  assign Units_U3__0 = 1'b0;
endmodule
